// Digital circuit main.dig as structural Verilog
module main (
  input  clk,
  output [5:0] out_2,
  output [1:0] out_3,
  output [5:0] out_4
);

  wire decoder_1_out_0, delay_1_out;

  Delay #(.delayTime(5)) delay_1 (.in(clk), .out(delay_1_out));
  Register #(.Bits(6)) register_1 (.D(out_2), .C(delay_1_out), .en(decoder_1_out_0), .Q(out_4));
  // instruction_memory instruction_memory_1: pin names not known; wires that end beside it: clk, out_3, out_2
  Decoder #(.Selector_Bits(2)) decoder_1 (.sel(out_3), .out_0(decoder_1_out_0));  // open: out_1, out_2, out_3
  RAMDualPort ramdualport_1 ();  // open: A, Din, str, C, ld, D

  // Notes on the sheet:
  //   LOAD
  //   STORE
  //   ADD
  //   SUB
endmodule
